# Fritzing sketch Tonino (saved by Fritzing 0.8.5b)

parts:
  Bauteil4 = TCS3200 Color Sensor
  Bauteil5 = DFRduino Nano V3
  7SEG2 = 7-Segment LED I2C Backpack (yellow)

nets:
  N1: Bauteil4.VDD, Bauteil5.D2
  GND: Bauteil4.GND#13, Bauteil4.OE, Bauteil5.GND, 7SEG2.GND
  N2: Bauteil4.LED, Bauteil4.GND#16, Bauteil5.D3
  N3: Bauteil4.S2, Bauteil5.D7
  N4: Bauteil4.S3, Bauteil5.D6
  N5: Bauteil4.OUT, Bauteil5.D5
  N6: Bauteil5.5V, 7SEG2.V+
  N7: Bauteil5.A5, 7SEG2.SCL
  N8: Bauteil5.A4, 7SEG2.SDA

notes:
  Tonino Hardware
  http://my-tonino.com

custom parts:
  TCS3200 Color Sensor: TCS3200 Color Sensor by DF Robot
  DFRduino Nano V3: The DFRduino Nano USB Microcontroller V3 (ATMega 328) is a breadboard ready version of the Arduino mini with integrated USB. The Nano has everything that the Diecimila has (electronically) with more analog input pins and an on-board +5V AREF jumper. The Nano automatically senses and switches to the higher power supply, so there is no need for a power select jumper. The nano's pin layout works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
  7-Segment LED I2C Backpack (yellow): 4-digit, 7-segment LED Display with I2C Control
